# Fritzing sketch doorsensor (saved by Fritzing 0.9.3b)
breadboards: 1

parts:
  U1 = ESP8266 WiFi Module [part_number=ESP8266]
  VCC1 = Battery block 9V
  R2 = Resistor [tolerance=±5% resistance=3.3k package="0603 [SMD]"]
  R3 = Resistor [tolerance=±5% resistance=3.3k package="0603 [SMD]"]
  R4 = Resistor [tolerance=±5% resistance=3.3k package="0603 [SMD]"]
  U2 = Voltage Regulator - 3.3V [package="TO220 [THT]"]
  J1 = Screw terminal - 2 pins [package=THT]
  S1 = Reed switch [package=THT]
  Q1 = TRANSISTOR_PNP [package=to-92]
  C1 = Electrolytic Capacitor [capacitance=100μF package="0807 [SMD, electrolytic]"]
  C2 = Electrolytic Capacitor [capacitance=10µF package="0807 [SMD, electrolytic]"]
  R5 = Resistor [tolerance=±5% resistance=3.3k package="0603 [SMD]"]
  J2 = Screw terminal - 2 pins [package=THT]
  R6 = Resistor [tolerance=±5% resistance=3.3k package="0603 [SMD]"]

nets:
  N1: U1.VCC, R3.Pin_1, R4.Pin_1, Q1.E, R5.Pin_1, R6.Pin_1
  N2: U1.GPIO_0, R6.Pin_0
  N3: U1.RST, R5.Pin_0
  N4: U1.GPIO_2, R4.Pin_0
  N5: U1.CH_PD, R3.Pin_0
  GND: U1.GND, VCC1.-, R2.Pin_1, U2.GND, C1.+, C2.-, J2.pin2
  N6: VCC1.+, U2.input_voltage, J1.pin2, S1.pin_2, C1.-, J2.pin1
  N7: R2.Pin_0, J1.pin1, S1.pin_1, Q1.B
  N8: U2.output_voltage, Q1.C, C2.+

custom parts:
  ESP8266 WiFi Module: Generic WiFi Module based on the ESP8266 with onboard PCB antenna and UART communications
