# Fritzing sketch esp-01_flashboard01 (saved by Fritzing 0.9.2b)
perfboards: 1

parts:
  J1 = single row smd female pin header, 5 pins [form="♀ (female)"]
  J2 = female pin header, 4 pins [form="♀ (female)"]
  J3 = female pin header, 4 pins [form="♀ (female)"]
  S1 = Pushbutton [package="[THT]"]
  S2 = Pushbutton [package="[THT]"]
  R2 = Resistor [tolerance=±20% resistance=10k package=THT]
  R3 = Resistor [tolerance=±20% resistance=10k package=THT]  # not connected
  R4 = Resistor [tolerance=±20% resistance=10k package=THT]

nets:
  N1: J1.pin1, J3.pin1
  N2: J1.pin2, J2.pin1
  N3: J1.pin3, J3.pin4
  N4: J1.pin5, J2.pin4, R2.Pin_1, R4.Pin_1
  N5: J2.pin3, S1.Pin_1, S1.Pin_2, R4.Pin_0
  N6: J3.pin3, S2.Pin_1, S2.Pin_2, R2.Pin_0
  N7: S1.Pin_3, S1.Pin_4, S2.Pin_3, S2.Pin_4
